# Fritzing sketch rp2040_spectrum_analyzer (saved by Fritzing 0.9.10b)
breadboards: 1

parts:
  Pico_H1 = Raspberry Pi Pico H
  S1 = Pushbutton [package="[THT]"]
  OLED1 = 128x32 I2C Monochrome OLED Display
  R1 = Resistor [tolerance=±5% power=0.25 resistance=10k package=THT]
  Mic_+_amp = Breakout Board for Electret Microphone

nets:
  3.3V: Pico_H1.VSYS, S1.Pin_1, S1.Pin_2, OLED1.3.3V, Mic_+_amp.VCC
  GND: Pico_H1.GND, OLED1.GND, R1.Pin_1, Mic_+_amp.GND
  N1: Pico_H1.GP26_A0, Mic_+_amp.AUD
  N2: Pico_H1.GP16, S1.Pin_3, S1.Pin_4, R1.Pin_0
  N3: Pico_H1.GP3, OLED1.SCL
  N4: Pico_H1.GP2, OLED1.SDA

custom parts:
  Raspberry Pi Pico H: Raspberry Pi Pico H. Based around the RP2040 microcontroller the Pico H is a low cost microcontroller device bringing Raspberry Pi quality, cost, and easy of use to the microcontroller space.
